// Logisim project regfile.circ as structural Verilog: 1 circuit, main circuit RegFile
module RegFile (
  input  [4:0] RD,
  input  [4:0] RS1,
  input  [4:0] RS2,
  input  [31:0] W,
  input  WE,
  input  Clk,
  output [31:0] s0,
  output [31:0] s1,
  output [31:0] t0,
  output [31:0] t1,
  output [31:0] a0,
  output [31:0] ra,
  output [31:0] sp,
  output [31:0] R1,
  output [31:0] R2
);

  wire [7:0] register_1_q, register_2_q, register_3_q, register_4_q, register_5_q, register_6_q,
       register_7_q, register_8_q, register_9_q;
  wire [7:1] WE_t;

  Register register_1 (.D({8{1'b0}}), .Q(register_1_q), .clk(Clk));  // open: en, clr
  Register register_2 (.D({WE_t, WE}), .Q(register_2_q), .clk(Clk));  // open: en, clr
  Register register_3 (.D({WE_t, WE}), .Q(register_3_q), .clk(Clk));  // open: en, clr
  Register register_4 (.D({WE_t, WE}), .Q(register_4_q), .clk(Clk));  // open: en, clr
  Register register_5 (.D({WE_t, WE}), .Q(register_5_q), .clk(Clk));  // open: en, clr
  Register register_6 (.D({WE_t, WE}), .Q(register_6_q), .clk(Clk));  // open: en, clr
  Register register_7 (.D({WE_t, WE}), .Q(register_7_q), .clk(Clk));  // open: en, clr
  Register register_8 (.D({WE_t, WE}), .Q(register_8_q), .clk(Clk));  // open: en, clr
  Register register_9 (.D({WE_t, WE}), .Q(register_9_q), .clk(Clk));  // open: en, clr
  Multiplexer #(.select(5), .width(8)) multiplexer_1 (
    .in0(register_1_q), .in1(register_2_q), .in2(register_3_q), .in3(register_4_q), .in4(register_5_q),
    .in5(register_6_q), .in6(register_7_q), .in7(register_8_q), .in8(register_9_q), .sel(RS1));  // open: in9, in10, in11, in12, in13, in14, in15, in16, in17, in18, in19, in20, in21, in22, in23, in24, in25, in26, in27, in28, in29, in30, in31, out, en
  Multiplexer #(.select(5), .width(8)) multiplexer_2 (
    .in0(register_1_q), .in1(register_2_q), .in2(register_3_q), .in3(register_4_q), .in4(register_5_q),
    .in5(register_6_q), .in6(register_7_q), .in7(register_8_q), .in8(register_9_q), .sel(RS2));  // open: in9, in10, in11, in12, in13, in14, in15, in16, in17, in18, in19, in20, in21, in22, in23, in24, in25, in26, in27, in28, in29, in30, in31, out, en
  // Pins of 1 and 8 bits meet at {WE_t, WE}

  // Other names for the same wires on the sheet: WE_t[0] = WE

  // Notes on the sheet:
  //   Write Register
  //   Read Register 1
  //   Read Register 2
  //   Write Data
  //   Write Enable
  //   Clock
  //   NOTE
  //   Please do not modify/replace/move/change/delete/etc input and output pins
  //   These are debug/test outputs from your circuit
  //   Read Data 1
  //   Read Data 2
endmodule
